// Digital circuit Address decoding.dig as structural Verilog
module Address_decoding (
  input  RIO,
  input  in_2,
  input  in_3,
  input  in_4,
  input  in_5,
  input  [15:0] ADDR
);

  wire _74138_1_pin9, _74138_1_pin15, _74138_2_pin7, _74138_2_pin9, _74138_2_pin10, _74138_2_pin11,
       _74138_2_pin12, _74138_2_pin13, _74138_2_pin14, _74138_2_pin15, _74139_1_pin4, _74139_1_pin5,
       _74139_1_pin6, _74139_1_pin7, _74139_1_pin9, _74139_1_pin10, _74139_1_pin11, _74139_1_pin12,
       and_1_out, and_2_out, nand_1_out, nand_2_out, nand_3_out, nand_4_out, nand_5_out, nor_1_out,
       nor_2_out, nor_3_out, nor_4_out, nor_5_out, nor_6_out, nor_7_out, nor_8_out, nor_9_out, not_1_out,
       not_2_out, not_3_out;

  not not_1 (not_1_out, ADDR[14]);
  nand nand_1 (nand_1_out, not_1_out, ADDR[15]);
  nand nand_2 (nand_2_out, ADDR[14], ADDR[15]);
  nor nor_1 (nor_1_out, ADDR[11], ADDR[10], ADDR[9]);
  nor nor_2 (nor_2_out, ADDR[8], ADDR[7], ADDR[6]);
  nor nor_3 (nor_3_out, ADDR[5], ADDR[4], ADDR[3]);
  nor nor_4 (nor_4_out, ADDR[2], ADDR[1], ADDR[0]);
  _74138 _74138_1 (
    .pin1(ADDR[12]), .pin2(ADDR[13]), .pin3(ADDR[14]), .pin4(ADDR[15]), .pin5(1'b0), .pin6(1'b1),
    .pin8(1'b0), .pin9(_74138_1_pin9), .pin15(_74138_1_pin15), .pin16(1'b1));  // open: pin7, pin10, pin11, pin12, pin13, pin14
  nand nand_3 (nand_3_out, nor_1_out, nor_2_out);
  nand nand_4 (nand_4_out, nor_3_out, nor_4_out);
  nor nor_5 (nor_5_out, _74138_1_pin15, nand_3_out, nand_4_out);
  not not_2 (not_2_out, nor_5_out);
  not not_3 (not_3_out, RIO);
  nor nor_6 (nor_6_out, _74138_1_pin9, RIO);
  _74138 _74138_2 (
    .pin1(ADDR[8]), .pin2(ADDR[9]), .pin3(ADDR[10]), .pin4(_74138_1_pin9), .pin5(ADDR[11]), .pin6(not_3_out),
    .pin7(_74138_2_pin7), .pin8(1'b0), .pin9(_74138_2_pin9), .pin10(_74138_2_pin10), .pin11(_74138_2_pin11),
    .pin12(_74138_2_pin12), .pin13(_74138_2_pin13), .pin14(_74138_2_pin14), .pin15(_74138_2_pin15),
    .pin16(1'b1));
  nor nor_7 (nor_7_out, _74138_1_pin9, RIO);
  nand nand_5 (nand_5_out, nor_7_out, ADDR[11]);
  _74139 _74139_1 (
    .pin1(nand_1_out), .pin2(in_4), .pin3(in_5), .pin4(_74139_1_pin4), .pin5(_74139_1_pin5),
    .pin6(_74139_1_pin6), .pin7(_74139_1_pin7), .pin8(1'b0), .pin9(_74139_1_pin9), .pin10(_74139_1_pin10),
    .pin11(_74139_1_pin11), .pin12(_74139_1_pin12), .pin13(in_3), .pin14(in_2), .pin15(nand_2_out),
    .pin16(1'b1));
  nor nor_8 (nor_8_out, nor_6_out, ADDR[15]);
  LED VIAB (.in(_74138_2_pin15));
  LED TFTB (.in(_74138_2_pin14));
  LED IO2B (.in(_74138_2_pin13));
  LED IO3B (.in(_74138_2_pin12));
  LED IO4B (.in(_74138_2_pin11));
  LED IO5B (.in(_74138_2_pin10));
  LED IO6B (.in(_74138_2_pin9));
  LED IO7B (.in(_74138_2_pin7));
  LED IOHB (.in(nand_5_out));
  nor nor_9 (nor_9_out, nor_8_out, nor_8_out);
  LED LORAMB (.in(nor_9_out));
  LED CTLREGB (.in(not_2_out));
  and and_1 (and_1_out, _74139_1_pin12, _74139_1_pin4);
  and and_2 (and_2_out, _74139_1_pin11, _74139_1_pin5);
  LED ROMB (.in(and_1_out));
  LED EXTH0B (.in(_74139_1_pin10));
  LED EXTH1B (.in(_74139_1_pin9));
  LED HIRAMB (.in(and_2_out));
  LED EXTL0B (.in(_74139_1_pin6));
  LED EXTL1B (.in(_74139_1_pin7));
endmodule
