// Digital circuit Buffer control.dig as structural Verilog
module Buffer_control (
  input  VIAB,
  input  ROMB,
  input  HIRAMB,
  input  LORAMB,
  input  EXTCTLB,
  input  RW
);

  wire and_1_out, and_2_out, and_3_out, xor_1_out, xor_2_out;

  and and_1 (and_1_out, VIAB, ROMB);
  and and_2 (and_2_out, HIRAMB, LORAMB);
  and and_3 (and_3_out, and_1_out, and_2_out);
  xor xor_1 (xor_1_out, EXTCTLB, and_3_out);
  xor xor_2 (xor_2_out, EXTCTLB, RW);
  LED OE (.in(xor_1_out));
  LED DDIR (.in(xor_2_out));
endmodule
