// Digital circuit Clock generation.dig as structural Verilog
module Clock_generation (
  input  clk,
  input  RSTB,
  input  SELCLK,
  input  D3,
  input  D2,
  input  D1,
  input  D0
);

  wire _74109_1_pin6, _74109_1_pin9, _74109_1_pin10, _74163_1_pin9, _74163_1_pin11, _74163_1_pin12,
       _74163_1_pin13, _74163_1_pin14, _74163_1_pin15, nor_1_out, nor_2_out, nor_3_out, nor_4_out, nor_5_out,
       nor_6_out, nor_7_out, nor_8_out, nor_9_out, nor_10_out, nor_11_out, nor_12_out;

  LED led_1 (.in(_74163_1_pin11));
  LED led_2 (.in(_74163_1_pin12));
  LED led_3 (.in(_74163_1_pin13));
  nor nor_1 (nor_1_out, nor_5_out, nor_5_out);
  nor nor_2 (nor_2_out, _74109_1_pin10, nor_5_out);
  nor nor_3 (nor_3_out, nor_1_out, SELCLK);
  LED led_4 (.in(_74163_1_pin14));
  _74163 _74163_1 (
    .pin1(RSTB), .pin2(clk), .pin3(D0), .pin4(D1), .pin5(D2), .pin6(D3), .pin7(1'b1), .pin8(1'b0),
    .pin9(_74163_1_pin9), .pin10(1'b1), .pin11(_74163_1_pin11), .pin12(_74163_1_pin12),
    .pin13(_74163_1_pin13), .pin14(_74163_1_pin14), .pin15(_74163_1_pin15), .pin16(1'b1));
  nor nor_4 (nor_4_out, nor_2_out, nor_3_out);
  xor xor_1 (_74163_1_pin9, 1'b1, _74163_1_pin15);
  nor nor_5 (nor_5_out, _74109_1_pin6, _74163_1_pin9);
  nor nor_6 (nor_6_out, clk, _74109_1_pin10);
  nor nor_7 (nor_7_out, _74109_1_pin6, _74109_1_pin9);
  _74109 _74109_1 (
    .pin1(1'b1), .pin2(_74163_1_pin15), .pin3(_74163_1_pin9), .pin4(clk), .pin5(1'b1), .pin6(_74109_1_pin6),
    .pin8(1'b0), .pin9(_74109_1_pin9), .pin10(_74109_1_pin10), .pin11(1'b1), .pin12(clk), .pin13(nor_4_out),
    .pin14(nor_4_out), .pin15(1'b1), .pin16(1'b1));  // open: pin7
  nor nor_8 (nor_8_out, nor_6_out, nor_7_out);
  nor nor_9 (nor_9_out, clk, clk);
  nor nor_10 (nor_10_out, _74109_1_pin6, _74109_1_pin6);
  nor nor_11 (nor_11_out, nor_9_out, nor_9_out);
  nor nor_12 (nor_12_out, nor_10_out, nor_10_out);
  LED CLKOSC (.in(nor_11_out));
  LED PHI2 (.in(nor_8_out));
  LED CLKDIV (.in(nor_12_out));

  // Notes on the sheet:
  //   clk: Hz: 5
endmodule
